// Logisim project cache.circ as structural Verilog: 2 circuits, main circuit cache
module cache (
  input  memRead,
  input  [7:0] address,
  input  [7:0] data_in,
  input  memWrite,
  input  clk,
  input  R,
  output miss,
  output [7:0] data_out
);

  wire demultiplexer_1_out0, demultiplexer_1_out1, demultiplexer_1_out2, demultiplexer_1_out3,
       demultiplexer_2_out0, demultiplexer_2_out1, demultiplexer_2_out2, demultiplexer_2_out3,
       demultiplexer_3_out0, demultiplexer_3_out1, demultiplexer_3_out2, demultiplexer_3_out3;
  wire [7:0] undriven, undriven_2, undriven_3, undriven_4;

  Demultiplexer #(.select(2)) demultiplexer_1 (
    .out0(demultiplexer_1_out0), .out1(demultiplexer_1_out1), .out2(demultiplexer_1_out2),
    .out3(demultiplexer_1_out3), .in(miss), .sel(address[3:2]));
  Demultiplexer #(.select(2)) demultiplexer_2 (
    .out0(demultiplexer_2_out0), .out1(demultiplexer_2_out1), .out2(demultiplexer_2_out2),
    .out3(demultiplexer_2_out3), .in(memRead), .sel(address[3:2]));
  Demultiplexer #(.select(2)) demultiplexer_3 (
    .out0(demultiplexer_3_out0), .out1(demultiplexer_3_out1), .out2(demultiplexer_3_out2),
    .out3(demultiplexer_3_out3), .in(memWrite), .sel(address[3:2]));
  cacheEntry cacheentry_1 (
    .miss(demultiplexer_1_out3), .memWrite(demultiplexer_3_out3), .tag(address[7:4]), .clk(clk),
    .data_in(data_in), .byte_offset(address[1:0]), .R(R), .memRead(demultiplexer_2_out3),
    .data_out(undriven_4));
  cacheEntry cacheentry_2 (
    .miss(demultiplexer_1_out2), .memWrite(demultiplexer_3_out2), .tag(address[7:4]), .clk(clk),
    .data_in(data_in), .byte_offset(address[1:0]), .memRead(demultiplexer_2_out2), .data_out(undriven_3));  // open: R
  cacheEntry cacheentry_3 (
    .miss(demultiplexer_1_out1), .memWrite(demultiplexer_3_out1), .tag(address[7:4]), .clk(clk),
    .data_in(data_in), .byte_offset(address[1:0]), .memRead(demultiplexer_2_out1), .data_out(undriven_2));  // open: R
  cacheEntry cacheentry_4 (
    .miss(demultiplexer_1_out0), .memWrite(demultiplexer_3_out0), .tag(address[7:4]), .clk(clk),
    .data_in(data_in), .byte_offset(address[1:0]), .R(R), .memRead(demultiplexer_2_out0), .data_out(undriven));
  Multiplexer #(.select(2), .width(8)) multiplexer_1 (
    .in0(undriven), .in1(undriven_2), .in2(undriven_3), .in3(undriven_4), .out(data_out), .sel(address[3:2]));

  // Other names for the same wires on the sheet: index[1:0] = address[3:2]

  // Notes on the sheet:
  //   offset
  //   index
  //   tag
endmodule

module cacheEntry (
  input  memRead,
  input  [3:0] tag,
  input  miss,
  input  clk,
  input  memWrite,
  input  [7:0] data_out,
  input  [1:0] byte_offset,
  input  [7:0] data_in,
  input  R
);

  wire comparator_1_eq, demultiplexer_1_out0, demultiplexer_1_out1, demultiplexer_1_out2,
       demultiplexer_1_out3, nand_1_out, or_1_out, validR_q;
  wire [3:0] tagR_q;
  wire [7:0] register_1_q, register_2_q, register_3_q, register_4_q;

  or or_1 (or_1_out, memWrite, miss);
  Demultiplexer #(.select(2)) demultiplexer_1 (
    .out0(demultiplexer_1_out0), .out1(demultiplexer_1_out1), .out2(demultiplexer_1_out2),
    .out3(demultiplexer_1_out3), .in(or_1_out), .sel(byte_offset));
  Register #(.width(1)) validR (.D(or_1_out), .en(or_1_out), .clk(clk), .Q(validR_q), .clr(R));
  Register #(.width(4)) tagR (.D(tag), .en(or_1_out), .clk(clk), .Q(tagR_q), .clr(R));
  Register register_1 (.D(data_in), .en(demultiplexer_1_out0), .clk(clk), .Q(register_1_q), .clr(R));
  Register register_2 (.D(data_in), .en(demultiplexer_1_out1), .clk(clk), .Q(register_2_q), .clr(R));
  Register register_3 (.D(data_in), .en(demultiplexer_1_out2), .clk(clk), .Q(register_3_q), .clr(R));
  Register register_4 (.D(data_in), .en(demultiplexer_1_out3), .clk(clk), .Q(register_4_q), .clr(R));
  Comparator #(.width(4)) comparator_1 (.a(tagR_q), .b(tag), .eq(comparator_1_eq));  // open: gt, lt
  Multiplexer #(.select(2), .width(8)) multiplexer_1 (
    .in0(register_1_q), .in1(register_2_q), .in2(register_3_q), .in3(register_4_q), .out(data_out),
    .sel(byte_offset));
  nand nand_1 (nand_1_out, validR_q, comparator_1_eq);
  and and_1 (miss, memRead, nand_1_out);
endmodule
